# Fritzing sketch CAD_drawing (saved by Fritzing 0.9.5d)
breadboards: 1

parts:
  Mod1 = Raspberry Pi 4B
  IC1 = Rasberry Pi NIOR Camera [chip_label=IC package="DIP (Dual Inline) [THT]"]  # not connected
  R1 = Resistor [tolerance=±5% resistance=2.2 package="0805 [SMD]"]
  R3 = Resistor [tolerance=±5% resistance=2.2 package="0603 [SMD]"]
  R2 = Resistor [tolerance=±5% resistance=2.2 package="0805 [SMD]"]
  R6 = Resistor [tolerance=±5% resistance=10k package="0805 [SMD]"]
  NchパワーMOSFET1 = MOSFET-NCHANNEL [part_number="60V25A 2SK2232\n" package=to220v]
  R7 = Resistor [tolerance=±5% resistance=10k package="0805 [SMD]"]
  R4 = Resistor [tolerance=±5% resistance=10 package="0805 [SMD]"]
  U1 = SWITCH_SPDT [package=kps-1290]
  5mm赤外線LE7 = smd LED [color="Infrared (940nm)" part_number=OSI5LA5A33A-B package="0805 [SMD]"]
  5mm赤外線LED4 = smd LED [color="Infrared (940nm)" part_number=OSI5LA5A33A-B package="0805 [SMD]"]
  5mm赤外線LED1 = smd LED [color="Infrared (940nm)" part_number=OSI5LA5A33A-B package="0805 [SMD]"]
  R5 = Resistor [tolerance=±5% resistance=100 package="0805 [SMD]"]
  赤外線リモコン受信モジュール = Infra red receiver [part_number="OSRB38C9AA\n"]
  5mm赤外線LED2 = smd LED [color="Infrared (940nm)" part_number=OSI5LA5A33A-B package="0805 [SMD]"]
  5mm赤外線LED3 = smd LED [color="Infrared (940nm)" part_number=OSI5LA5A33A-B package="0805 [SMD]"]
  5mm赤外線LED6 = smd LED [color="Infrared (940nm)" part_number=OSI5LA5A33A-B package="0805 [SMD]"]
  5mm赤外線LED8 = smd LED [color="Infrared (940nm)" part_number=OSI5LA5A33A-B package="0805 [SMD]"]
  5mm赤外線LED9 = smd LED [color="Infrared (940nm)" part_number=OSI5LA5A33A-B package="0805 [SMD]"]
  S2 = Momentary Switch [package=ksa_sealed_tac_switch]
  3mmレッドLED2 = LED - 3mm [color="Red (635nm)" package="3 mm [THT]"]
  5mm赤外線LED5 = smd LED [color="Infrared (940nm)" part_number=OSI5LA5A33A-B package="0805 [SMD]"]
  NchパワーMOSFET2 = MOSFET-NCHANNEL [part_number="60V25A 2SK2232\n" package=to220v]
  D1 = Rectifier Diode [part_number=1N5819 package="Melf DO-213 AA [SMD]"]

nets (from the schematic view):
  N1: Mod1.5V, U1.P
  GND: Mod1.GND, R6.Pin_0, NchパワーMOSFET1.S, R7.Pin_0, 赤外線リモコン受信モジュール.GND, NchパワーMOSFET2.S
  N2: Mod1.GPIO23, NchパワーMOSFET1.G, R7.Pin_1
  N3: Mod1.GPIO25, 赤外線リモコン受信モジュール.Data
  N4: Mod1.GPIO8, R6.Pin_1, NchパワーMOSFET2.G
  N5: R1.Pin_0, R3.Pin_0, R2.Pin_0, R4.Pin_0, U1.O
  N6: R1.Pin_1, 5mm赤外線LED1.anode
  N7: R3.Pin_1, 5mm赤外線LE7.anode
  N8: R2.Pin_1, 5mm赤外線LED4.anode
  N9: NchパワーMOSFET1.D, S2.1, S2.2, 3mmレッドLED2.cathode
  N10: R4.Pin_1, R5.Pin_0
  N11: U1.S, 赤外線リモコン受信モジュール.VCC
  N12: 5mm赤外線LE7.cathode, 5mm赤外線LED8.anode
  N13: 5mm赤外線LED4.cathode, 5mm赤外線LED5.anode
  N14: 5mm赤外線LED1.cathode, 5mm赤外線LED2.anode
  N15: R5.Pin_1, 3mmレッドLED2.anode
  N16: 5mm赤外線LED2.cathode, 5mm赤外線LED3.anode
  N17: 5mm赤外線LED3.cathode, 5mm赤外線LED6.cathode, 5mm赤外線LED9.cathode, NchパワーMOSFET2.D, D1.cathode
  N18: 5mm赤外線LED6.anode, 5mm赤外線LED5.cathode
  N19: 5mm赤外線LED8.cathode, 5mm赤外線LED9.anode
  N20: S2.3, S2.4, D1.anode

custom parts:
  Rasberry Pi NIOR Camera: Camera
  Momentary Switch: Momentary Switch Button commonly used for reset or general input. Spark Fun Electronics SKU : COM-00097
